# Fritzing sketch Zeldaduino (saved by Fritzing 0.9.4)
breadboards: 1

parts:
  Bauteil1 = Arduino Nano (Rev3.0)
  DFRobot_DFPlayer_Mini1 = DFRobot DFPlayer Mini [part_number=DFR0299]
  R1 = PHOTOCELL [package=photocell-kit]
  J1 = Piezo Speaker
  R2 = Resistor [tolerance=±5% resistance=1k package=THT]

nets:
  N1: Bauteil1.GND, DFRobot_DFPlayer_Mini1.GND-1, DFRobot_DFPlayer_Mini1.GND-2
  N2: Bauteil1.D2, R1.P$1
  N3: Bauteil1.D10, DFRobot_DFPlayer_Mini1.TX
  N4: Bauteil1.D11/MOSI, R2.Pin_0
  5V: Bauteil1.5V, DFRobot_DFPlayer_Mini1.VCC
  N5: Bauteil1.3V3, R1.P$2
  N6: DFRobot_DFPlayer_Mini1.RX, R2.Pin_1
  N7: DFRobot_DFPlayer_Mini1.SPK_1, J1.pin2
  N8: DFRobot_DFPlayer_Mini1.SPK_2, J1.pin1
